// Logisim project sap2_main.circ as structural Verilog: 1 circuit, main circuit main
module main (
  input  in_1,
  input  in_2,
  input  in_3,
  input  in_4,
  input  in_5,
  input  in_6,
  input  in_7,
  input  in_8,
  input  in_9,
  input  in_10,
  input  in_11,
  input  in_12,
  input  in_13,
  input  in_14,
  input  in_15,
  input  in_16,
  input  in_17,
  input  in_18,
  input  in_19,
  input  in_20,
  input  in_21,
  input  in_22,
  input  in_23,
  input  in_24,
  input  in_25,
  input  in_26,
  input  in_27,
  input  in_28,
  input  in_29,
  input  in_30,
  input  in_31,
  input  in_32,
  input  in_33,
  input  in_34,
  input  in_35,
  input  in_36,
  output [15:0] out_37,
  output [15:0] out_38,
  output [15:0] out_39
);

  wire arithmetic_logic_unit_1_p6, arithmetic_logic_unit_1_p7, nor_1_out;
  wire [7:0] ram_1_dout, register_8_1_q1, register_8_2_o1, register_8_3_o1;
  wire [15:0] register_16_1_q1;

  RAM #(.addrWidth(16), .asyncread("true")) ram_1 (
    .addr(register_16_1_q1), .we(in_19), .oe(in_20), .clk(in_21), .din(register_8_1_q1), .dout(ram_1_dout));
  pc pc_1 (.EN(in_4), .LOAD(in_5), .COUNT(in_6), .CLK(in_7), .D_in(out_37), .Q_out(out_37), .O_out(out_38));
  register_16 register_16_1 (
    .D1(out_37[0]), .D2(out_37[1]), .D3(out_37[2]), .D4(out_37[3]), .D5(out_37[4]), .D6(out_37[5]),
    .D7(out_37[6]), .D8(out_37[7]), .D9(out_37[8]), .D10(out_37[9]), .D11(out_37[10]), .D12(out_37[11]),
    .D13(out_37[12]), .D14(out_37[13]), .D15(out_37[14]), .D16(out_37[15]), .LOAD(in_13), .CLK(in_14),
    .EN(in_15), .O1(out_39[0]), .O2(out_39[1]), .O3(out_39[2]), .O4(out_39[3]), .O5(out_39[4]),
    .O6(out_39[5]), .O7(out_39[6]), .O8(out_39[7]), .O9(out_39[8]), .O10(out_39[9]), .O11(out_39[10]),
    .O12(out_39[11]), .O13(out_39[12]), .O14(out_39[13]), .O15(out_39[14]), .O16(out_39[15]),
    .Q1(register_16_1_q1[0]), .Q2(register_16_1_q1[1]), .Q3(register_16_1_q1[2]), .Q4(register_16_1_q1[3]),
    .Q5(register_16_1_q1[4]), .Q6(register_16_1_q1[5]), .Q7(register_16_1_q1[6]), .Q8(register_16_1_q1[7]),
    .Q9(register_16_1_q1[8]), .Q10(register_16_1_q1[9]), .Q11(register_16_1_q1[10]),
    .Q12(register_16_1_q1[11]), .Q13(register_16_1_q1[12]), .Q14(register_16_1_q1[13]),
    .Q15(register_16_1_q1[14]), .Q16(register_16_1_q1[15]));
  register_8 register_8_1 (
    .D1(ram_1_dout[0]), .D2(ram_1_dout[1]), .D3(ram_1_dout[2]), .D4(ram_1_dout[3]), .D5(ram_1_dout[4]),
    .D6(ram_1_dout[5]), .D7(ram_1_dout[6]), .D8(ram_1_dout[7]), .LOAD(in_22), .CLK(in_23), .EN(in_24),
    .Q1(register_8_1_q1[0]), .Q2(register_8_1_q1[1]), .Q3(register_8_1_q1[2]), .Q4(register_8_1_q1[3]),
    .Q5(register_8_1_q1[4]), .Q6(register_8_1_q1[5]), .Q7(register_8_1_q1[6]), .Q8(register_8_1_q1[7]));  // open: O1, O2, O3, O4, O5, O6, O7, O8
  Demultiplexer #(.tristate("true"), .width(8)) demultiplexer_1 (
    .out0(out_37[7:0]), .out1(out_37[15:8]), .in(register_8_1_q1), .sel(in_25));
  register_z16bits register_z16bits_1 (
    .D1(out_37[0]), .D2(out_37[1]), .D3(out_37[2]), .D4(out_37[3]), .D5(out_37[4]), .D6(out_37[5]),
    .D7(out_37[6]), .D8(out_37[7]), .D9(out_37[8]), .D10(out_37[9]), .D11(out_37[10]), .D12(out_37[11]),
    .D13(out_37[12]), .D14(out_37[13]), .D15(out_37[14]), .D16(out_37[15]), .CLK(in_29), .LOAD1(in_30),
    .LOAD2(in_31), .EN1(in_32), .EN2(in_33), .Q1(out_37[0]), .Q2(out_37[1]), .Q3(out_37[2]), .Q4(out_37[3]),
    .Q5(out_37[4]), .Q6(out_37[5]), .Q7(out_37[6]), .Q8(out_37[7]), .Q9(out_37[8]), .Q10(out_37[9]),
    .Q11(out_37[10]), .Q12(out_37[11]), .Q13(out_37[12]), .Q14(out_37[13]), .Q15(out_37[14]), .Q16(out_37[15]));  // open: O1, O2, O3, O4, O5, O6, O7, O8, O9, O10, O11, O12, O13, O14, O15, O16
  register_8 register_8_2 (
    .D1(out_37[0]), .D2(out_37[1]), .D3(out_37[2]), .D4(out_37[3]), .D5(out_37[4]), .D6(out_37[5]),
    .D7(out_37[6]), .D8(out_37[7]), .LOAD(in_1), .CLK(in_2), .EN(in_3), .O1(register_8_2_o1[0]),
    .O2(register_8_2_o1[1]), .O3(register_8_2_o1[2]), .O4(register_8_2_o1[3]), .O5(register_8_2_o1[4]),
    .O6(register_8_2_o1[5]), .O7(register_8_2_o1[6]), .O8(register_8_2_o1[7]), .Q1(out_37[0]),
    .Q2(out_37[1]), .Q3(out_37[2]), .Q4(out_37[3]), .Q5(out_37[4]), .Q6(out_37[5]), .Q7(out_37[6]),
    .Q8(out_37[7]));
  register_8 register_8_3 (
    .D1(out_37[0]), .D2(out_37[1]), .D3(out_37[2]), .D4(out_37[3]), .D5(out_37[4]), .D6(out_37[5]),
    .D7(out_37[6]), .D8(out_37[7]), .LOAD(in_16), .CLK(in_17), .EN(in_18), .O1(register_8_3_o1[0]),
    .O2(register_8_3_o1[1]), .O3(register_8_3_o1[2]), .O4(register_8_3_o1[3]), .O5(register_8_3_o1[4]),
    .O6(register_8_3_o1[5]), .O7(register_8_3_o1[6]), .O8(register_8_3_o1[7]), .Q1(out_37[0]),
    .Q2(out_37[1]), .Q3(out_37[2]), .Q4(out_37[3]), .Q5(out_37[4]), .Q6(out_37[5]), .Q7(out_37[6]),
    .Q8(out_37[7]));
  register_8 register_8_4 (
    .D1(out_37[0]), .D2(out_37[1]), .D3(out_37[2]), .D4(out_37[3]), .D5(out_37[4]), .D6(out_37[5]),
    .D7(out_37[6]), .D8(out_37[7]), .LOAD(in_26), .CLK(in_27), .EN(in_28), .Q1(out_37[0]), .Q2(out_37[1]),
    .Q3(out_37[2]), .Q4(out_37[3]), .Q5(out_37[4]), .Q6(out_37[5]), .Q7(out_37[6]), .Q8(out_37[7]));  // open: O1, O2, O3, O4, O5, O6, O7, O8
  register_8 register_8_5 (
    .D1(out_37[0]), .D2(out_37[1]), .D3(out_37[2]), .D4(out_37[3]), .D5(out_37[4]), .D6(out_37[5]),
    .D7(out_37[6]), .D8(out_37[7]), .LOAD(in_34), .CLK(in_35), .EN(in_36), .Q1(out_37[0]), .Q2(out_37[1]),
    .Q3(out_37[2]), .Q4(out_37[3]), .Q5(out_37[4]), .Q6(out_37[5]), .Q7(out_37[6]), .Q8(out_37[7]));  // open: O1, O2, O3, O4, O5, O6, O7, O8
  // arithmetic_logic_unit arithmetic_logic_unit_1: pin names not known; wires that end beside it: register_8_2_o1, register_8_3_o1, in_8, in_9, in_10, arithmetic_logic_unit_1_p6, arithmetic_logic_unit_1_p7, out_37[7:0]
  nor nor_1 (nor_1_out, out_37[0], out_37[1], out_37[2], out_37[3], out_37[4], out_37[5], out_37[6], out_37[7]);

  // Notes on the sheet:
  //   Random Access Memory
  //   Memory Address Register
  //   Memory Data Register
  //   Accumulator Register
  //   Temporary Register
  //   Register B
  //   Register C
endmodule
